# Fritzing sketch FSPLRXVK16PFZYU (saved by Fritzing 0.9.3b)

parts:
  S1 = H-Bridge with L298N
  Raspberry_Pi_1 = Raspberry Pi 3 [part_number=RPI-3-V1.2]
  M1 = DC Motor
  M3 = DC Motor
  M2 = DC Motor  # not connected

nets:
  GND: S1.GND, Raspberry_Pi_1.GND
  N1: S1.ENA, Raspberry_Pi_1.GPIO22
  N2: S1.IN1, Raspberry_Pi_1.GPIO17
  N3: S1.IN2, Raspberry_Pi_1.GPIO27
  N4: S1.IN3, Raspberry_Pi_1.GPIO23
  N5: S1.IN4, Raspberry_Pi_1.GPIO24
  N6: S1.ENB, Raspberry_Pi_1.GPIO25
  N7: S1.M1-01, M1.pin_2
  N8: S1.M1-02, M1.pin_1
  N9: S1.M2-01, M3.pin_2
  N10: S1.M2-02, M3.pin_1

notes:
  Steering Motor
  Throttle Motors
  To LiPo Battery

custom parts:
  H-Bridge with L298N: h-bridge
